// Digital circuit core.dig as structural Verilog
module core (
  input  in_1
);

  wire clk, control_1_brinst, control_1_jal_jalr, dmwen, immreg, pcjump, rfwen, rs1pc;
  wire [1:0] wbsel;
  wire [2:0] func3;
  wire [4:0] instdecoder_1_p2, instdecoder_1_p3, instdecoder_1_p4;
  wire [6:0] func7;
  wire [31:0] aluout, imm, immunit_1_imm, inst, multiplexer_1_out, multiplexer_2_out, notconnected_1_out,
       outdm, pc, pc4, rd1, rd2, res;

  Multiplexer #(.Bits(32)) multiplexer_1 (.sel(pcjump), .in_0(pc4), .in_1(aluout), .out(multiplexer_1_out));
  // pc pc_1: pin names not known; wires that end beside it: multiplexer_1_out, 1'b1, in_1, clk, pc
  Add #(.Bits(32)) add_1 (.a(pc), .b(32'h4), .c_i(1'b0), .s(pc4));  // open: c_o
  pmemory pmemory_1 (.addr(pc), .inst(inst));
  // instdecoder instdecoder_1: pin names not known; wires that end beside it: inst, instdecoder_1_p2, instdecoder_1_p3, instdecoder_1_p4, func3, func7
  control control_1 (
    .Inst(inst), .Imm_reg(immreg), .rfwenable(rfwen), .dmwenable(dmwen), .brinst(control_1_brinst),
    .jal_jalr(control_1_jal_jalr), .WBsel(wbsel));
  registerfile registerfile_1 (
    .enable(rfwen), .rdAdrs(instdecoder_1_p2), .rdData(res), .rs1Adrs(instdecoder_1_p3),
    .rs2Adrs(instdecoder_1_p4), .clock(clk), .rs1Data(rd1), .rs2Data(rd2));
  immunit immunit_1 (.Inst(inst), .imm(immunit_1_imm));
  bjunit bjunit_1 (
    .rs1data(rd1), .rs2data(rd2), .binst(control_1_brinst), .func3(func3), .jal(control_1_jal_jalr),
    .pcjump(pcjump), .rs1pc(rs1pc));
  Multiplexer #(.Bits(32)) multiplexer_2 (.sel(rs1pc), .in_0(rd1), .in_1(pc), .out(multiplexer_2_out));
  Multiplexer #(.Bits(32)) multiplexer_3 (.sel(immreg), .in_0(rd2), .in_1(immunit_1_imm), .out(imm));
  alucomp alucomp_1 (.op_1(multiplexer_2_out), .op_2(imm), .f3(func3), .f7(func7), .out(aluout));
  // Probe on pc
  // Probe on res
  // Probe on outdm
  // Probe on inst
  // Probe on imm
  // Probe on wbsel
  dmemory dmemory_1 (.clk(clk), .dmwen(dmwen), .func3(func3), .wdata(rd2), .addr(aluout), .out(outdm));
  Button button_1 (.out(clk));
  Multiplexer #(.Selector_Bits(2), .Bits(32)) multiplexer_4 (
    .sel(wbsel), .in_0(aluout), .in_1(outdm), .in_2(pc4), .in_3(notconnected_1_out), .out(res));
  // NotConnected on notconnected_1_out

  // Other names for the same wires on the sheet: reset = in_1
endmodule
