// Digital circuit dmemory.dig as structural Verilog
module dmemory (
  input  clk,
  input  dmwen,
  input  [2:0] func3,
  input  [31:0] wdata,
  input  [31:0] addr,
  output [31:0] out
);

  wire and_1_out, and_2_out, and_3_out, Byte_eq, Half_eq, lbyte, lhalf, lword;
  wire [7:0] byte0, byte1, byte2, byte3;

  and and_1 (and_1_out, dmwen, lbyte);
  Comparator #(.Bits(3)) Byte (.a(func3), .b(3'b000), .eq(Byte_eq));  // open: gt, lt
  Comparator #(.Bits(3)) Half (.a(func3), .b(3'b001), .eq(Half_eq));  // open: gt, lt
  Comparator #(.Bits(3)) Word (.a(func3), .b(3'b010), .eq(lword));  // open: gt, lt
  BlockRAMDualPort #(.AddrBits(24), .Bits(8)) blockramdualport_1 (
    .A(addr[23:0]), .Din(wdata[7:0]), .str(and_1_out), .C(clk), .D(byte0));
  and and_2 (and_2_out, dmwen, lhalf);
  or or_1 (lbyte, Byte_eq, Half_eq, lword);
  or or_2 (lhalf, lword, Half_eq);
  BlockRAMDualPort #(.AddrBits(24), .Bits(8)) blockramdualport_2 (
    .A(addr[23:0]), .Din(wdata[15:8]), .str(and_2_out), .C(clk), .D(byte1));
  and and_3 (and_3_out, dmwen, lword);
  BlockRAMDualPort #(.AddrBits(24), .Bits(8)) blockramdualport_3 (
    .A(addr[23:0]), .Din(wdata[23:16]), .str(and_3_out), .C(clk), .D(byte2));
  Multiplexer #(.Bits(8)) multiplexer_1 (.sel(lbyte), .in_0({8{1'b0}}), .in_1(byte0), .out(out[7:0]));
  Multiplexer #(.Bits(8)) multiplexer_2 (.sel(lhalf), .in_0({8{1'b0}}), .in_1(byte1), .out(out[15:8]));
  Multiplexer #(.Bits(8)) multiplexer_3 (.sel(lword), .in_0({8{1'b0}}), .in_1(byte2), .out(out[23:16]));
  Multiplexer #(.Bits(8)) multiplexer_4 (.sel(lword), .in_0({8{1'b0}}), .in_1(byte3), .out(out[31:24]));
  BlockRAMDualPort #(.AddrBits(24), .Bits(8)) blockramdualport_4 (
    .A(addr[23:0]), .Din(wdata[31:24]), .str(and_3_out), .C(clk), .D(byte3));

  // Other names for the same wires on the sheet: addr_t[23:0] = addr[23:0]; dat0_7[7:0] = wdata[7:0];
  //   dat8_15[7:0] = wdata[15:8]; dat16_23[7:0] = wdata[23:16]; dat24_31[7:0] = wdata[31:24]
endmodule
